// Logisim project Arith_unit.circ as structural Verilog: 1 circuit, main circuit main
module main (
  input  [31:0] in_1,
  input  in_2,
  input  [31:0] in_3,
  output [31:0] out_4
);

  wire [31:0] ANDOUT, SUBOUT;

  Adder #(.width(32)) adder_1 (.a(in_1), .b(in_3), .out(ANDOUT));  // open: cin, cout
  Subtractor #(.width(32)) subtractor_1 (.a(in_1), .b(in_3), .out(SUBOUT));  // open: bin, bout
  Multiplexer #(.width(32), .enable("false")) multiplexer_1 (.in0(ANDOUT), .in1(SUBOUT), .out(out_4), .sel(in_2));

  // Other names for the same wires on the sheet: IN1[31:0] = in_1; IN2[31:0] = in_3

  // Notes on the sheet:
  //   add
  //   sub
endmodule
