// Logisim project IF_ID.circ as structural Verilog: 1 circuit, main circuit main
module main (
  input  [31:0] in_1,
  input  [31:0] in_2,
  input  [31:0] in_3,
  input  [19:0] in_4,
  input  in_5,
  output [31:0] out_6,
  output [31:0] out_7,
  output [19:0] out_8
);

  wire undriven_2, undriven_3, undriven_4;
  wire [31:0] Instruction_q, undriven;

  Register #(.width(20)) PC_Branch (.D(in_4), .en(1'b1), .clk(in_5), .Q(out_8));  // open: clr
  Register #(.width(32)) Instruction (
    .D(undriven), .en(undriven_2), .Q(Instruction_q), .clk(undriven_3), .clr(undriven_4));
  Register #(.width(32)) Instruction_2 (
    .D(undriven), .en(undriven_2), .Q(Instruction_q), .clk(undriven_3), .clr(undriven_4));
  Register #(.width(32)) PC_Register (.D(in_1), .en(1'b1), .clk(in_5), .Q(out_6));  // open: clr

  assign in_3 = in_2;

  // Other names for the same wires on the sheet: Branch[19:0] = out_8; Instruction[31:0] = in_2;
  //   Next_pc[31:0] = out_6; pc_1[31:0] = in_1; PC_Branch[19:0] = in_4; sub_instruction[31:0] = out_7
endmodule
