// Logisim project Inst_memory.circ as structural Verilog
module main (
  input  [19:0] in_1,
  output [5:0] out_2,
  output [4:0] out_3,
  output [4:0] out_4,
  output [4:0] out_5,
  output [10:0] out_6,
  output [15:0] out_7
);

  ROM #(.addrWidth(20), .dataWidth(32)) rom_1 (.addr(in_1), .data({out_6, out_5, out_4, out_3, out_2}));

  assign out_7 = {out_6, out_5};

  // Other names for the same wires on the sheet: op[5:0] = out_2; d_ImmL[4:0] = out_3; S1[4:0] = out_4;
  //   Imm16[15:0] = {out_6, out_5}; S2[4:0] = out_5; F_ImmU[10:0] = out_6; PC[19:0] = in_1
endmodule
