// Logisim project PC.circ as structural Verilog: 1 circuit, main circuit main
module main (
  input  [31:0] in_1,
  input  [10:0] in_2,
  input  [15:0] in_3,
  input  in_4,
  input  [4:0] in_5,
  input  in_6,
  input  [19:0] in_7,
  input  in_8,
  output [31:0] out_9,
  output [19:0] out_10,
  output [19:0] out_11
);

  wire adder_2_cout;
  wire [19:0] adder_4_out, bit_extender_2_out, bit_extender_3_out, multiplexer_1_out, multiplexer_2_out,
       PC_11;

  assign out_9 = {{12{1'b0}}, PC_11};  // Bit_Extender bit_extender_1
  Register #(.width(20)) PC_Register (.D(multiplexer_2_out), .en(1'b1), .clk(in_4), .Q(out_10));  // open: clr
  assign bit_extender_2_out = {{4{in_2[10]}}, {in_2, in_5}};  // Bit_Extender bit_extender_2
  Adder #(.width(20)) adder_1 (.a(out_10), .b(20'h1), .out(PC_11), .cin(1'b0));  // open: cout
  Adder #(.width(20)) adder_2 (.a(out_10), .b(bit_extender_2_out), .out(out_11), .cin(1'b0), .cout(adder_2_cout));
  Adder #(.width(20)) adder_3 (.a(out_10), .b(bit_extender_2_out), .out(out_11), .cin(1'b0), .cout(adder_2_cout));
  assign bit_extender_3_out = {{4{in_3[15]}}, in_3};  // Bit_Extender bit_extender_3
  Adder #(.width(20)) adder_4 (.a(bit_extender_3_out), .b(in_1[19:0]), .out(adder_4_out), .cin(1'b0));  // open: cout
  Multiplexer #(.width(20), .enable("false")) multiplexer_1 (
    .in0(PC_11), .in1(in_7), .out(multiplexer_1_out), .sel(in_6));
  Multiplexer #(.width(20), .enable("false")) multiplexer_2 (
    .in0(multiplexer_1_out), .in1(adder_4_out), .out(multiplexer_2_out), .sel(in_8));

  // Other names for the same wires on the sheet: ImmL[4:0] = in_5; ImmU[10:0] = in_2; Address[19:0] = out_10;
  //   clock = in_4; Imm16[15:0] = in_3; PC_1[31:0] = out_9; pc_branch[19:0] = out_11; RS1[31:0] = in_1
endmodule
